# Fritzing sketch mvp (saved by Fritzing 0.9.3b)

parts:
  Part1 = Arduino Nano (Rev3.0)
  Raspberry_Pi_1 = Raspberry Pi 3 [part_number=RPI-3-V1.2]
  U1 = DC-DC_CONVERTER [package=dc-dc_converter]
  S1 = Pushbutton [package="[SMD]"]
  Part2 = Arduino Nano (Rev3.0)
  U2 = LIPO-2000mAh [package=lipo-2000]
  F1 = FUSE [package=fuse_5mm]
  F2 = FUSE [package=fuse_5mm]

nets:
  N1: Part1.VIN, F1.2
  N2: Part1.GND, S1.Pin_3, S1.Pin_4, U2.-
  N3: Raspberry_Pi_1.GPIO2, Raspberry_Pi_1.5V, U1.VOUT, U1.SENSE
  GND: Raspberry_Pi_1.GPIO3, Raspberry_Pi_1.GIPO14, Raspberry_Pi_1.GND, U1.GND1
  N4: U1.ON_OFF, U1.VIN, F2.2
  N5: S1.Pin_1, S1.Pin_2, Part2.D2, Part2.D3
  N6: Part2.RESET, Part2.GND
  N7: U2.+, F1.1, F2.1

notes:
  Motorcycle battery
  12V - 14V
  Output: 5V 3A
  Time synchronizer
  Ext interupt: 2, 3, 9, 10, 11, 13, A1, A5, A7
  https://www.arduino.cc/reference/en/language/functions/external-interrupts/attachinterrupt/
  D2 INPUT_PULLUP
